// Digital circuit bf_cpu_with_preprocessor.dig as structural Verilog
module bf_cpu_with_preprocessor (
  input  clk
);

  wire _8b_or_1_or, and_1_out, and_2_out, comparator_1_eq, delay_1_out, delay_2_out, delay_3_out, not_1_out,
       not_2_out, one_time_bit_1_exc, one_time_bit_1_pc_plus__plus, one_time_bit_1_rst, or_1_out, or_2_out,
       or_3_out;
  wire [7:0] ascii_2_opcode_out, BF_Program_d, bf_rle_instruction_encoder_1_rleopc, counter_1_out,
       prev_opc_q, xor_1_out;
  wire [15:0] PC_2_out, PC_out;

  one_time_bit one_time_bit_1 (
    .Cl(clk), .Rst(one_time_bit_1_rst), .Exc(one_time_bit_1_exc), .PC_plus__plus(one_time_bit_1_pc_plus__plus));
  Counter #(.Bits(16)) PC (.en(1'b1), .C(one_time_bit_1_exc), .clr(1'b0), .out(PC_out));  // open: ovf
  EEPROMDualPort #(.AddrBits(16), .isProgramMemory("true"), .Bits(8)) BF_Program (
    .A(PC_out), .Din({8{1'b0}}), .str(1'b0), .C(one_time_bit_1_pc_plus__plus), .ld(1'b1), .D(BF_Program_d));
  LookUpTable #(.Bits(8)) ascii_2_opcode (
    .in0(BF_Program_d[0]), .in1(BF_Program_d[1]), .in2(BF_Program_d[2]), .in3(BF_Program_d[3]),
    .in4(BF_Program_d[4]), .in5(BF_Program_d[5]), .in6(BF_Program_d[6]), .in7(BF_Program_d[7]),
    .out(ascii_2_opcode_out));
  Delay #(.delayTime(8)) delay_1 (.in(one_time_bit_1_pc_plus__plus), .out(delay_1_out));
  or or_1 (or_1_out, one_time_bit_1_rst, one_time_bit_1_pc_plus__plus);
  or or_2 (or_2_out, delay_1_out, and_1_out);
  Register #(.Bits(8)) prev_opc (.D(ascii_2_opcode_out), .C(or_1_out), .en(1'b1), .Q(prev_opc_q));
  Counter #(.Bits(8)) counter_1 (.en(delay_1_out), .C(or_2_out), .clr(and_1_out), .out(counter_1_out));  // open: ovf
  Comparator #(.Bits(8)) comparator_1 (.a(8'h1), .b(prev_opc_q), .eq(comparator_1_eq));  // open: gt, lt
  not not_1 (not_1_out, comparator_1_eq);
  assign xor_1_out = ascii_2_opcode_out ^ prev_opc_q;  // XOr xor_1, 8 bits wide
  _8b_or _8b_or_1 (.\byte (xor_1_out), .\or (_8b_or_1_or));
  and and_1 (and_1_out, not_2_out, _8b_or_1_or);
  not not_2 (not_2_out, one_time_bit_1_rst);
  Delay #(.delayTime(2)) delay_2 (.in(not_1_out), .out(delay_2_out));
  and and_2 (and_2_out, delay_2_out, and_1_out);
  Delay #(.delayTime(4)) delay_3 (.in(one_time_bit_1_rst), .out(delay_3_out));
  or or_3 (or_3_out, and_2_out, delay_3_out);
  bf_rle_instruction_encoder bf_rle_instruction_encoder_1 (
    .Opc(prev_opc_q), .Count(counter_1_out), .RLEopc(bf_rle_instruction_encoder_1_rleopc));
  CounterPreset #(.Bits(16)) PC_2 (
    .en(and_2_out), .C(or_3_out), .dir(1'b0), .in({16{1'b0}}), .ld(1'b0), .clr(delay_3_out), .out(PC_2_out));  // open: ovf
  RAMDualPort #(.AddrBits(16), .Bits(8)) RLE_program (
    .A(PC_2_out), .Din(bf_rle_instruction_encoder_1_rleopc), .str(and_2_out), .C(and_2_out), .ld(1'b1));  // open: D

  // Notes on the sheet:
  //   Reset
  //   PC++
  //   Exec
  //   Program iterator
  //   contents of BF_Program (hex, n*v repeats v):
  //   a,a,2b,2b,2b,2b,2b,2b,2b,2b,2b,2b,2b,2b,2b,5b,2d,3e,2b,2b,3e,3e,3e,2b,2b,2b,2b,2b,
  //   3e,2b,2b,3e,2b,3c,3c,3c,3c,3c,3c,5d,3e,3e,3e,3e,3e,2b,2b,2b,2b,2b,2b,3e,2d,2d,2d,
  //   3e,3e,3e,3e,3e,3e,3e,3e,3e,3e,2b,2b,2b,2b,2b,2b,2b,2b,2b,2b,2b,2b,2b,2b,2b,5b,5b,
  //   3e,3e,3e,3e,3e,3e,3e,3e,3e,5d,2b,5b,3c,3c,3c,3c,3c,3c,3c,3c,3c,5d,3e,3e,3e,3e,3e,
  //   3e,3e,3e,3e,2d,5d,2b,5b,3e,3e,3e,3e,3e,3e,3e,3e,5b,2d,5d,3e,5d,3c,3c,3c,3c,3c,3c,
  //   3c,3c,3c,5b,3c,3c,3c,3c,3c,3c,3c,3c,3c,5d,3e,3e,3e,3e,3e,3e,3e,3e,5b,2d,5d,2b,3c,
  //   3c,3c,3c,3c,3c,3c,2b,2b,2b,2b,2b,5b,2d,5b,2d,3e,3e,3e,3e,3e,3e,3e,3e,3e,2b,3c,3c,
  //   3c,3c,3c,3c,3c,3c,3c,5d,3e,3e,3e,3e,3e,3e,3e,3e,3e,5d,3e,3e,3e,3e,3e,3e,3e,2b,3e,
  //   3e,3e,3e,3e,3e,3e,3e,3e,3e,3e,3e,3e,3e,3e,3e,3e,3e,3e,3e,3e,3e,3e,3e,3e,3e,3e,2b,
  //   3c,3c,3c,3c,3c,3c,3c,3c,3c,3c,3c,3c,3c,3c,3c,3c,3c,5b,3c,3c,3c,3c,3c,3c,3c,3c,3c,
  //   5d,3e,3e,3e,5b,2d,5d,2b,5b,3e,3e,3e,3e,3e,3e,5b,3e,3e,3e,3e,3e,3e,3e,5b,2d,5d,3e,
  //   3e,5d,3c,3c,3c,3c,3c,3c,3c,3c,3c,5b,3c,3c,3c,3c,3c,3c,3c,3c,3c,5d,3e,3e,3e,3e,3e,
  //   3e,3e,5b,2d,5d,2b,3c,3c,3c,3c,3c,3c,2b,2b,2b,2b,5b,2d,5b,2d,3e,3e,3e,3e,3e,3e,3e,
  //   3e,3e,2b,3c,3c,3c,3c,3c,3c,3c,3c,3c,5d,3e,3e,3e,3e,3e,3e,3e,3e,3e,5d,3e,3e,3e,3e,
  //   3e,3e,2b,3c,3c,3c,3c,3c,3c,2b,2b,2b,2b,2b,2b,2b,5b,2d,5b,2d,3e,3e,3e,3e,3e,3e,3e,
  //   3e,3e,2b,3c,3c,3c,3c,3c,3c,3c,3c,3c,5d,3e,3e,3e,3e,3e,3e,3e,3e,3e,5d,3e,3e,3e,3e,
  //   3e,3e,2b,3c,3c,3c,3c,3c,3c,3c,3c,3c,3c,3c,3c,3c,3c,3c,3c,5b,3c,3c,3c,3c,3c,3c,3c,
  //   3c,3c,5d,3e,3e,3e,5b,5b,2d,5d,3e,3e,3e,3e,3e,3e,5b,3e,3e,3e,3e,3e,3e,3e,5b,2d,3c,
  //   3c,3c,3c,3c,3c,2b,3e,3e,3e,3e,3e,3e,5d,3c,3c,3c,3c,3c,3c,5b,2d,3e,3e,3e,3e,3e,3e,
  //   2b,3c,3c,2b,3c,3c,3c,2b,3c,5d,3e,3e,3e,3e,3e,3e,3e,3e,5d,3c,3c,3c,3c,3c,3c,3c,3c,
  //   3c,5b,3c,3c,3c,3c,3c,3c,3c,3c,3c,5d,3e,3e,3e,3e,3e,3e,3e,3e,3e,5b,3e,3e,3e,3e,3e,
  //   3e,3e,3e,5b,2d,3c,3c,3c,3c,3c,3c,3c,2b,3e,3e,3e,3e,3e,3e,3e,5d,3c,3c,3c,3c,3c,3c,
  //   3c,5b,2d,3e,3e,3e,3e,3e,3e,3e,2b,3c,3c,2b,3c,3c,3c,2b,3c,3c,5d,3e,3e,3e,3e,3e,3e,
  //   3e,3e,5d,3c,3c,3c,3c,3c,3c,3c,3c,3c,5b,3c,3c,3c,3c,3c,3c,3c,3c,3c,5d,3e,3e,3e,3e,
  //   3e,3e,3e,5b,2d,3c,3c,3c,3c,3c,3c,3c,2b,3e,3e,3e,3e,3e,3e,3e,5d,3c,3c,3c,3c,3c,3c,
  //   3c,5b,2d,3e,3e,3e,3e,3e,3e,3e,2b,3c,3c,2b,3c,3c,3c,3c,3c,5d,3e,3e,3e,3e,3e,3e,3e,
  //   3e,3e,2b,2b,2b,2b,2b,2b,2b,2b,2b,2b,2b,2b,2b,2b,2b,5b,5b,3e,3e,3e,3e,3e,3e,3e,3e,
  //   3e,5d,2b,3e,5b,2d,5d,3e,5b,2d,5d,3e,5b,2d,5d,3e,5b,2d,5d,3e,5b,2d,5d,3e,5b,2d,5d,
  //   3e,5b,2d,5d,3e,5b,2d,5d,3e,5b,2d,5d,3c,3c,3c,3c,3c,3c,3c,3c,3c,5b,3c,3c,3c,3c,3c,
  //   3c,3c,3c,3c,5d,3e,3e,3e,3e,3e,3e,3e,3e,3e,2d,5d,2b,5b,3e,2b,3e,3e,3e,3e,3e,3e,3e,
  //   3e,5d,3c,3c,3c,3c,3c,3c,3c,3c,3c,5b,3c,3c,3c,3c,3c,3c,3c,3c,3c,5d,3e,3e,3e,3e,3e,
  //   3e,3e,3e,3e,5b,3e,2d,3e,3e,3e,3e,5b,2d,3c,3c,3c,3c,2b,3e,3e,3e,3e,5d,3c,3c,3c,3c,
  //   5b,2d,3e,3e,3e,3e,2b,3c,3c,3c,3c,3c,5b,2d,3e,3e,5b,2d,3c,3c,2b,3e,3e,5d,3c,3c,5b,
  //   2d,3e,3e,2b,3e,3e,2b,3c,3c,3c,3c,5d,2b,3e,3e,3e,3e,3e,3e,3e,3e,3e,5d,3c,3c,3c,3c,
  //   3c,3c,3c,3c,5b,3c,3c,3c,3c,3c,3c,3c,3c,3c,5d,5d,3e,3e,3e,3e,3e,3e,3e,3e,3e,5b,3e,
  //   3e,3e,3e,3e,3e,3e,3e,3e,5d,3c,3c,3c,3c,3c,3c,3c,3c,3c,5b,3e,5b,2d,3e,3e,3e,3e,3e,
  //   3e,3e,3e,3e,2b,3c,3c,3c,3c,3c,3c,3c,3c,3c,5d,3c,3c,3c,3c,3c,3c,3c,3c,3c,3c,5d,3e,
  //   5b,2d,3e,3e,3e,3e,3e,3e,3e,3e,3e,2b,3c,3c,3c,3c,3c,3c,3c,3c,3c,5d,3c,2b,3e,3e,3e,
  //   3e,3e,3e,3e,3e,5d,3c,3c,3c,3c,3c,3c,3c,3c,3c,5b,3e,5b,2d,5d,3c,2d,3e,3e,3e,3e,5b,
  //   2d,3c,3c,3c,3c,2b,3e,5b,3c,2d,3e,2d,3c,3c,3c,3c,3c,3c,2b,3e,3e,3e,3e,3e,3e,5d,3c,
  //   5b,2d,3e,2b,3c,5d,3e,3e,3e,3e,5d,3c,3c,3c,5b,2d,3e,3e,3e,2b,3c,3c,3c,5d,3c,2b,3c,
  //   3c,3c,3c,3c,3c,3c,3c,3c,5d,3e,3e,3e,3e,3e,3e,3e,3e,3e,5b,3e,2b,3e,3e,3e,3e,3e,3e,
  //   3e,3e,5d,3c,3c,3c,3c,3c,3c,3c,3c,3c,5b,3c,3c,3c,3c,3c,3c,3c,3c,3c,5d,3e,3e,3e,3e,
  //   3e,3e,3e,3e,3e,5b,3e,2d,3e,3e,3e,3e,3e,5b,2d,3c,3c,3c,3c,3c,2b,3e,3e,3e,3e,3e,5d,
  //   3c,3c,3c,3c,3c,5b,2d,3e,3e,3e,3e,3e,2b,3c,3c,3c,3c,3c,3c,5b,2d,3e,3e,3e,5b,2d,3c,
  //   3c,3c,2b,3e,3e,3e,5d,3c,3c,3c,5b,2d,3e,3e,3e,2b,3e,2b,3c,3c,3c,3c,5d,2b,3e,3e,3e,
  //   3e,3e,3e,3e,3e,3e,5d,3c,3c,3c,3c,3c,3c,3c,3c,5b,3c,3c,3c,3c,3c,3c,3c,3c,3c,5d,5d,
  //   3e,3e,3e,3e,3e,3e,3e,3e,3e,5b,3e,3e,3e,3e,3e,3e,3e,3e,3e,5d,3c,3c,3c,3c,3c,3c,3c,
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  //   Clock2
  //   Clock1
  //   Opcode
  //   contents of ascii_2_opcode (hex, n*v repeats v):
  //   1,1,1,1,1,1,1,1,1,1,1,1,1,1,1,1,1,1,1,1,1,1,1,1,1,1,1,1,1,1,1,1,1,1,1,1,1,1,1,1,1,
  //   1,1,2b,80,2d,c0,1,1,1,1,1,1,1,1,1,1,1,1,1,3c,1,3e,1,1,1,1,1,1,1,1,1,1,1,1,1,1,1,1,
  //   1,1,1,1,1,1,1,1,1,1,1,1,0,1,40,1,1,1,1,1,1,1,1,1,1,1,1,1,1,1,1,1,1,1,1,1,1,1,1,1,
  //   1,1,1,1,1,1,1,1,1,1,1,1,1,1,1,1,1,1,1,1,1,1,1,1,1,1,1,1,1,1,1,1,1,1,1,1,1,1,1,1,1,
  //   1,1,1,1,1,1,1,1,1,1,1,1,1,1,1,1,1,1,1,1,1,1,1,1,1,1,1,1,1,1,1,1,1,1,1,1,1,1,1,1,1,
  //   1,1,1,1,1,1,1,1,1,1,1,1,1,1,1,1,1,1,1,1,1,1,1,1,1,1,1,1,1,1,1,1,1,1,1,1,1,1,1,1,1,
  //   1,1,1,1,1,1,1,1,1,1,1,1,1,1
  //   is valid opcode
  //   opcode changed
endmodule
